# Fritzing sketch Schematics Pondus (saved by Fritzing 0.9.3b)

parts:
  3_3v_8MHz_Arduino = Arduino Pro Mini (3.3V)
  220_mAh_3_7v_Li-ion = LIPO-110mAh [package=lipo-110]
  Battery_charger_with_USB_connector = USB LiPoly Charger
  Pulse_sensor_module = mystery part, 3 pins [chip_label=Heart]
  LED_for_stress_output = LEDs [package=led10mm]

nets:
  N1: 3_3v_8MHz_Arduino.VCC, 220_mAh_3_7v_Li-ion.+, Battery_charger_with_USB_connector.VBAT, Pulse_sensor_module.pin1
  GND: 3_3v_8MHz_Arduino.GND, 220_mAh_3_7v_Li-ion.-, Battery_charger_with_USB_connector.GND, Pulse_sensor_module.pin3, LED_for_stress_output.C
  N2: 3_3v_8MHz_Arduino.A0, Pulse_sensor_module.pin2
  N3: 3_3v_8MHz_Arduino.D5, LED_for_stress_output.A
